// Logisim project alarme_v1.circ as structural Verilog: 1 circuit, main circuit main
module main (
  input  A,
  input  B,
  input  C
);

  wire and_1_out, or_1_out;

  or or_1 (or_1_out, A, B);
  LED D (.in(C));
  and and_1 (and_1_out, or_1_out, C);
  LED S (.in(and_1_out));

  // Notes on the sheet:
  //   A = Detecta se a porta esta aberta 
  //   B = Detecta movimentação no ambiente
  //   C = chave de ativação do sistema
  //   S = Alarme 0/1
endmodule
